// Digital circuit main.dig as structural Verilog
module main (
  input  clk
);

  wire C, P_out, S_out, str_REG;
  wire [2:0] instr_decode_1_funct3;
  wire [4:0] instr_decode_1_rd, instr_decode_1_rs1, instr_decode_1_rs2;
  wire [6:0] instr_decode_1_funct7, instr_decode_1_opcode;
  wire [15:0] Exceptions;
  wire [31:0] add_1_s, immediate_generation_1_p2, memory_1_instr, pc_1_pc, registers_1_d_1;

  PC pc_1 (.C(C), .PC(pc_1_pc));
  Memory memory_1 (
    .Addr({32{1'b0}}), .D_in({32{1'b0}}), .PC(pc_1_pc), .C(C), .str(1'b0), .ld(1'b0), .Instr(memory_1_instr),
    .Except(Exceptions));  // open: D_out
  instr_decode instr_decode_1 (
    .I(memory_1_instr), .opcode(instr_decode_1_opcode), .funct3(instr_decode_1_funct3),
    .funct7(instr_decode_1_funct7), .rd(instr_decode_1_rd), .rs1(instr_decode_1_rs1), .rs2(instr_decode_1_rs2));  // open: csr, imm_csr
  control control_1 (
    .opcode(instr_decode_1_opcode), .funct3(instr_decode_1_funct3), .funct7(instr_decode_1_funct7),
    .str_REG(str_REG), .Except(Exceptions));
  Registers registers_1 (
    .C(C), .str(str_REG), .A_d(instr_decode_1_rd), .A_s1(instr_decode_1_rs1), .A_s2(instr_decode_1_rs2),
    .D(add_1_s), .D_1(registers_1_d_1));  // open: D_2
  // immediate_generation immediate_generation_1: pin names not known; wires that end beside it: memory_1_instr, immediate_generation_1_p2
  Button P (.out(P_out));
  Button S (.out(S_out));
  Add #(.Bits(32)) add_1 (.a(registers_1_d_1), .b(immediate_generation_1_p2), .c_i(1'b0), .s(add_1_s));  // open: c_o
  LED Store_AMO_Page_Fault (.in(Exceptions[15]));
  LED led_1 (.in(Exceptions[14]));
  LED Load_Page_Fault (.in(Exceptions[13]));
  LED Instruction_Page_Fault (.in(Exceptions[12]));
  LED Environment_Call_From_M_mode (.in(Exceptions[11]));
  LED led_2 (.in(Exceptions[10]));
  LED Environment_Call_From_S_mode (.in(Exceptions[9]));
  LED Environment_Call_From_U_mode (.in(Exceptions[8]));
  LED Store_AMO_Access_Fault (.in(Exceptions[7]));
  LED Store_AMO_Address_Misaligned (.in(Exceptions[6]));
  LED Load_Access_Fault (.in(Exceptions[5]));
  LED Load_Address_Misaligned (.in(Exceptions[4]));
  LED Breakpoint (.in(Exceptions[3]));
  LED Illegal_Instruction (.in(Exceptions[2]));
  LED Instruction_Access_Fault (.in(Exceptions[1]));
  LED Instruction_Address_Misaligned (.in(Exceptions[0]));
  Clock #(.generic("Scale := 50;")) clock_1 (.C_in(clk), .Start_Stop(P_out), .Step(S_out), .C(C));

  // Notes on the sheet:
  //   clk: Hz: 50
endmodule
