// Digital circuit Memory.dig as structural Verilog
module Memory (
  input  [31:0] PC,
  input  [31:0] D_in,
  input  [31:0] Addr,
  input  C,
  input  str,
  input  ld,
  output [31:0] Instr,
  output [31:0] D_out,
  output [15:0] Except
);

  wire equals_zero_1_eq_0, equals_zero_2_eq_0, not_1_out, or_1_out, or_2_out;
  wire [1:0] notconnected_5_out;
  wire [7:0] button_1_out, notconnected_6_out;

  and and_1 (Except[6], str, or_1_out);
  or or_1 (or_1_out, Addr[0], Addr[1]);
  or or_2 (or_2_out, PC[1], PC[0]);
  LED led_1 (.in(Except[4]));
  LED led_2 (.in(Except[6]));
  and and_2 (Except[4], or_1_out, ld);
  equals_zero #(.generic("Bits := 6;")) equals_zero_1 (.X(Addr[31:26]), .eq_0(equals_zero_1_eq_0));
  equals_zero #(.generic("Bits := 6;")) equals_zero_2 (.X(PC[31:26]), .eq_0(equals_zero_2_eq_0));
  LED led_3 (.in(or_2_out));
  LED led_4 (.in(Except[7]));
  and and_3 (Except[7], str, not_1_out);
  LED led_5 (.in(Except[5]));
  LED led_6 (.in(Except[1]));
  and and_4 (Except[5], not_1_out, ld);
  not not_1 (not_1_out, equals_zero_1_eq_0);
  // NotConnected on Except[0]
  // NotConnected on Except[3:2]
  // NotConnected on Except[15:8]
  not not_2 (Except[1], equals_zero_2_eq_0);
  RAMDualAccess #(.AddrBits(24), .isProgramMemory("true"), .Bits(32)) ramdualaccess_1 (
    .str(str), .C(C), .ld(ld), .A1(Addr[25:2]), .Din1(D_in), .A2(PC[25:2]), .D1(D_out), .D2(Instr));
  Button button_1 (.out(button_1_out[1]));
  Button button_2 (.out(button_1_out[4]));
  Button button_3 (.out(button_1_out[5]));
  Button button_4 (.out(button_1_out[6]));
  Button button_5 (.out(button_1_out[7]));
  // NotConnected on button_1_out[0]
  // NotConnected on notconnected_5_out
  // NotConnected on notconnected_6_out
  // Probe on {notconnected_6_out, button_1_out[7:4], notconnected_5_out, button_1_out[1:0]}

  // Notes on the sheet:
  //   Note: Instruction address
  //   misaligned is not output
  //   here because it is raised
  //   on the jump instead of on
  //   the load.
  //   Load Address Misaligned
  //   Store Address Misaligned
  //   Instruction Address Misaligned
  //   Store/AMO Access Fault
  //   Load Access Fault
  //   Instruction Access Fault
endmodule

/* Test case Write one cell:
C str ld Addr D_in PC D_out Instr SAM LAM SAF LAF IAF

declare SAM = (Except >> 6) & 1;
declare LAM = (Except >> 4) & 1;
declare SAF = (Except >> 7) & 1;
declare LAF = (Except >> 5) & 1;
declare IAF = (Except >> 1) & 1;

0 0   0  0    0    0  z     0     0   0   0   0   0
0 0   1  0    0    0  0     0     0   0   0   0   0
0 0   1  4    0    0  0     0     0   0   0   0   0
0 0   1  0    0    4  0     0     0   0   0   0   0
C 0   1  0    5    4  0     0     0   0   0   0   0
0 1   1  0    5    4  0     0     0   0   0   0   0
C 1   1  0    5    4  5     0     0   0   0   0   0
0 0   1  4    0    0  0     5     0   0   0   0   0
C 1   1  0    0    0  0     0     0   0   0   0   0
*/

/* Test case Write full RAM:
	C str ld Addr      D_in    PC        D_out   Instr   SAM LAM SAF LAF IAF

declare SAM = (Except >> 6) & 1;
declare LAM = (Except >> 4) & 1;
declare SAF = (Except >> 7) & 1;
declare LAF = (Except >> 5) & 1;
declare IAF = (Except >> 1) & 1;

# Write some of the RAM
loop(a, 1<<16)
	0 0   1  (a << 10) (a + 5) 4         0       0       0   0   0   0   0
	C 1   1  (a << 10) (a + 5) 4         (a + 5) 0       0   0   0   0   0
end loop

# Read the data through Addr
loop(a, 1<<16)
	0 0   1  (a << 10) 0       4         (a + 5) 0       0   0   0   0   0
end loop

# Read the data through PC
loop(a, 1<<16)
	0 0   1  4         0       (a << 10) 0       (a + 5) 0   0   0   0   0
end loop
*/

/* Test case Preload program:
	C str ld Addr D_in PC   D_out      Instr SAM LAM SAF LAF IAF

declare SAM = (Except >> 6) & 1;
declare LAM = (Except >> 4) & 1;
declare SAF = (Except >> 7) & 1;
declare LAF = (Except >> 5) & 1;
declare IAF = (Except >> 1) & 1;

program(0x5A5A5A5A, 0xA5A5A5A5, 0x0, 0x1, 0xFFFFFFFF)
	0 0   1  0    0    40   0x5A5A5A5A 0     0   0   0   0   0
	0 0   1  4    0    40   0xA5A5A5A5 0     0   0   0   0   0
	0 0   1  8    0    40   0x0        0     0   0   0   0   0
	0 0   1  12   0    40   0x1        0     0   0   0   0   0
	0 0   1  16   0    40   0xFFFFFFFF 0     0   0   0   0   0
	0 0   1  20   0    40   0          0     0   0   0   0   0
*/

/* Test case Misaligned:
C str ld Addr D_in PC D_out Instr SAM LAM SAF LAF IAF

declare SAM = (Except >> 6) & 1;
declare LAM = (Except >> 4) & 1;
declare SAF = (Except >> 7) & 1;
declare LAF = (Except >> 5) & 1;
declare IAF = (Except >> 1) & 1;

0 0   0  0    0    0  z     0     0   0   0   0   0
# Test LAM (load address misaligned)
0 0   1  0    0    0  0     0     0   0   0   0   0
0 0   1  1    0    0  0     0     0   1   0   0   0
0 0   1  2    0    0  0     0     0   1   0   0   0
0 0   1  3    0    0  0     0     0   1   0   0   0
0 0   1  4    0    0  0     0     0   0   0   0   0
0 0   1  5    0    0  0     0     0   1   0   0   0
0 0   1  6    0    0  0     0     0   1   0   0   0
0 0   1  7    0    0  0     0     0   1   0   0   0
0 0   1  8    0    0  0     0     0   0   0   0   0
0 0   1  9    0    0  0     0     0   1   0   0   0
0 0   1  10   0    0  0     0     0   1   0   0   0
0 0   1  11   0    0  0     0     0   1   0   0   0

# Test SAM (store address misaligned)
0 1  0   0    0    0  z     0     0   0   0   0   0
0 1  0   1    0    0  z     0     1   0   0   0   0
0 1  0   2    0    0  z     0     1   0   0   0   0
0 1  0   3    0    0  z     0     1   0   0   0   0
0 1  0   4    0    0  z     0     0   0   0   0   0
0 1  0   5    0    0  z     0     1   0   0   0   0
0 1  0   6    0    0  z     0     1   0   0   0   0
0 1  0   7    0    0  z     0     1   0   0   0   0
0 1  0   8    0    0  z     0     0   0   0   0   0
0 1  0   9    0    0  z     0     1   0   0   0   0
0 1  0   10   0    0  z     0     1   0   0   0   0
0 1  0   11   0    0  z     0     1   0   0   0   0
*/

/* Test case Out of range:
	C str ld Addr D_in PC  D_out Instr SAM LAM SAF LAF IAF

declare SAM = (Except >> 6) & 1;
declare LAM = (Except >> 4) & 1;
declare SAF = (Except >> 7) & 1;
declare LAF = (Except >> 5) & 1;
declare IAF = (Except >> 1) & 1;

# Write random addresses
loop(i, 10000)
	# Generate random addresss >= (1 << 26)
	let a = (((random(7) + 1) << 26) + (random(1 << 24) << 2));

	0 1   0  (a)  0    0   z     0     0   0   1   0   0
	0 0   1  (a)  0    0   0     0     0   0   0   1   0
	0 0   0  0    0    (a) z     0     0   0   0   0   1
end loop
*/
