// Digital circuit Clock.dig as structural Verilog
module Clock (
  input  C_in,
  input  Start_Stop,
  input  Step,
  output C
);

  wire comparator_1_eq, t_ff_1_q, t_ff_2_q, xor_1_out;
  wire [31:0] counter_1_out;

  T_FF t_ff_1 (.T(1'b1), .C(Start_Stop), .Q(t_ff_1_q));  // open: nQ
  xor xor_1 (xor_1_out, C_in, comparator_1_eq);
  Counter #(.Bits(32)) counter_1 (
    .en(t_ff_1_q), .C(xor_1_out), .clr(comparator_1_eq), .out(counter_1_out));  // open: ovf
  Comparator #(.Bits(32)) comparator_1 (.a(32'h32), .b(counter_1_out), .eq(comparator_1_eq));  // open: gt, lt
  // Probe on counter_1_out
  T_FF t_ff_2 (.T(1'b1), .C(comparator_1_eq), .Q(t_ff_2_q));  // open: nQ
  xor xor_2 (C, t_ff_2_q, Step);

  // Notes on the sheet:
  //   C_in: Hz: 50
endmodule

/* Code that sets the parameters or builds the circuit:
Scale := 50;
*/

/* Test case No scaling:
	C_in Start/Stop Step C
# Disabled by default
loop(i, 10)
	0    0          0    0
end loop

# Enable => flips every cycle
	0    C          0    0
loop(i, 10)
	C    0          0    1
	C    0          0    0
end loop

# Disable
	0    C          0    0
loop(i, 10)
	C    0          0    0
end loop

# Use step
loop(i, 10)
	0    0          1    1
	0    0          0    0
end loop

# Run for one cycle
	0    C          0    0
	C    0          0    1
	0    C          0    1

# Step works inverted
loop(i, 10)
	0    0          0    1
	0    0          1    0
end loop
*/

/* Test case Scale 2:
	C_in Start/Stop Step C
# Disabled by default
loop(i, 20)
	0    0          0    0
end loop

# Enable => flips every other cycle
	0    C          0    0
loop(i, 10)
	C    0          0    0
	C    0          0    1
	C    0          0    1
	C    0          0    0
end loop

# Disable
	0    C          0    0
loop(i, 20)
	C    0          0    0
end loop
*/

/* Test case Scale 5:
	C_in Start/Stop Step C
# Disabled by default
loop(i, 50)
	0    0          0    0
end loop

# Enable => flips every other cycle
	0    C          0    0
loop(i, 10)
	C    0          0    0
	C    0          0    0
	C    0          0    0
	C    0          0    0
	C    0          0    1
	C    0          0    1
	C    0          0    1
	C    0          0    1
	C    0          0    1
	C    0          0    0
end loop

# Disable
	0    C          0    0
loop(i, 50)
	C    0          0    0
end loop
*/
