// Digital circuit Registers.dig as structural Verilog
module Registers (
  input  C,
  input  str,
  input  [4:0] A_s1,
  input  [4:0] A_s2,
  input  [4:0] A_d,
  input  [31:0] D,
  output [31:0] D_1,
  output [31:0] D_2
);

  wire equals_zero_1_eq_0, equals_zero_2_eq_0;
  wire [31:0] registerfile_1_da, registerfile_1_db;

  RegisterFile #(.AddrBits(5), .Bits(32)) registerfile_1 (
    .Din(D), .we(str), .Rw(A_d), .C(C), .Ra(A_s1), .Rb(A_s2), .Da(registerfile_1_da), .Db(registerfile_1_db));
  equals_zero #(.generic("Bits := 5;")) equals_zero_1 (.X(A_s1), .eq_0(equals_zero_1_eq_0));
  equals_zero #(.generic("Bits := 5;")) equals_zero_2 (.X(A_s2), .eq_0(equals_zero_2_eq_0));
  Multiplexer #(.Bits(32)) multiplexer_1 (
    .sel(equals_zero_1_eq_0), .in_0(registerfile_1_da), .in_1({32{1'b0}}), .out(D_1));
  Multiplexer #(.Bits(32)) multiplexer_2 (
    .sel(equals_zero_2_eq_0), .in_0(registerfile_1_db), .in_1({32{1'b0}}), .out(D_2));
endmodule

/* Test case:
	C str A_s1  A_s2  A_d  D    D_1    D_2
# Initially empty, remain empty without stores
loop(i,32)
	0 0   (i)   (i)   (i)  (i)  0      0
	0 1   (i)   (i)   (i)  (i)  0      0
	C 0   (i)   (i)   (i)  (i)  0      0
end loop

# Store (-i) in each register
loop(i, 32)
	C 1   0     0     (i)  (-i) 0      0
end loop

# x0 remains 0
	0 0   0      0     0   0    0      0

# Read (-i) from each register using s1 and s2
loop(i, 31)
	0 0   (i+1) 0      0   0    (-i-1) 0
	0 0   0     (i+1)  0   0    0      (-i-1)
end loop
*/
