// Digital circuit control.dig as structural Verilog
module control (
  input  [6:0] opcode,
  input  [2:0] funct3,
  input  [6:0] funct7,
  output str_REG,
  output [15:0] Except
);

  wire [1:1] Control_ROM_d;

  ROM #(.AddrBits(17), .Bits(2)) Control_ROM (
    .A({opcode, funct3, funct7}), .sel(1'b1), .D({Control_ROM_d[1], str_REG}));
  LED led_1 (.in(Control_ROM_d[1]));
  // NotConnected on Except[1:0]
  // NotConnected on Except[15:3]
  assign Except[2] = Control_ROM_d[1] ? 1'b1 : 1'bz;  // Driver driver_1
  PullDown pulldown_1 (.out(Except[2]));

  // Notes on the sheet:
  //   Control_ROM loads control.bin
  //   Illegal Instruction
endmodule

/* Test case:
	opcode    funct3 funct7    str_REG II
# Get illegal instruction bit
declare II = (Except >> 2) & 1;

# addi
loop(f7, (1 << 7))
	0b0010011 0b000  (f7)      1       0
end loop

# Some illegal instructions
	0b0000000 0b000  0b0000000 0       1
	0b1111111 0b111  0b1111111 0       1
	0b0111010 0b001  0b0011001 0       1
*/
