// Digital circuit immediate_generation.dig as structural Verilog
module immediate_generation (
  input  [31:0] I,
  output [31:0] imm_I,
  output [31:0] imm_S,
  output [31:0] imm_B,
  output [31:0] imm_U,
  output [31:0] imm_J
);

  BitExtender #(.inputBits(12), .outputBits(32)) bitextender_1 (.in(I[31:20]), .out(imm_I));
  BitExtender #(.inputBits(12), .outputBits(32)) bitextender_2 (.in({I[31:25], I[11:7]}), .out(imm_S));
  BitExtender #(.inputBits(13), .outputBits(32)) bitextender_3 (
    .in({I[31], I[7], I[30:25], I[11:8], 1'b0}), .out(imm_B));
  BitExtender #(.inputBits(21), .outputBits(32)) bitextender_4 (
    .in({I[31], I[19:12], I[20], I[30:21], 1'b0}), .out(imm_J));

  assign imm_U = {I[31:12], {12{1'b0}}};
endmodule

/* Test case Every bit:
I       imm-I      imm-S      imm-B      imm-U      imm-J
0       0          0          0          0          0
(1<<0)  0          0          0          0          0
(1<<1)  0          0          0          0          0
(1<<2)  0          0          0          0          0
(1<<3)  0          0          0          0          0
(1<<4)  0          0          0          0          0
(1<<5)  0          0          0          0          0
(1<<6)  0          0          0          0          0
(1<<7)  0          0x00000001 0x00000800 0          0
(1<<8)  0          0x00000002 0x00000002 0          0
(1<<9)  0          0x00000004 0x00000004 0          0
(1<<10) 0          0x00000008 0x00000008 0          0
(1<<11) 0          0x00000010 0x00000010 0          0
(1<<12) 0          0          0          0x00001000 0x00001000
(1<<13) 0          0          0          0x00002000 0x00002000
(1<<14) 0          0          0          0x00004000 0x00004000
(1<<15) 0          0          0          0x00008000 0x00008000
(1<<16) 0          0          0          0x00010000 0x00010000
(1<<17) 0          0          0          0x00020000 0x00020000
(1<<18) 0          0          0          0x00040000 0x00040000
(1<<19) 0          0          0          0x00080000 0x00080000
(1<<20) 0x00000001 0          0          0x00100000 0x00000800
(1<<21) 0x00000002 0          0          0x00200000 0x00000002
(1<<22) 0x00000004 0          0          0x00400000 0x00000004
(1<<23) 0x00000008 0          0          0x00800000 0x00000008
(1<<24) 0x00000010 0          0          0x01000000 0x00000010
(1<<25) 0x00000020 0x00000020 0x00000020 0x02000000 0x00000020
(1<<26) 0x00000040 0x00000040 0x00000040 0x04000000 0x00000040
(1<<27) 0x00000080 0x00000080 0x00000080 0x08000000 0x00000080
(1<<28) 0x00000100 0x00000100 0x00000100 0x10000000 0x00000100
(1<<29) 0x00000200 0x00000200 0x00000200 0x20000000 0x00000200
(1<<30) 0x00000400 0x00000400 0x00000400 0x40000000 0x00000400
(1<<31) 0xFFFFF800 0xFFFFF800 0xFFFFF000 0x80000000 0xFFF00000
*/
