// Digital circuit instr_decode.dig as structural Verilog
module instr_decode (
  input  [31:0] I,
  output [6:0] opcode,
  output [2:0] funct3,
  output [6:0] funct7,
  output [4:0] rd,
  output [4:0] rs1,
  output [4:0] rs2,
  output [11:0] csr,
  output [31:0] imm_csr
);


  assign csr = I[31:20];
  assign funct3 = I[14:12];
  assign funct7 = I[31:25];
  assign imm_csr = {{27{1'b0}}, I[19:15]};
  assign opcode = I[6:0];
  assign rd = I[11:7];
  assign rs1 = I[19:15];
  assign rs2 = I[24:20];
endmodule

/* Test case Every bit:
I       opcode    funct3 funct7    rd      rs1     rs2     imm-csr csr
0       0b0000000 0      0         0       0       0       0       0
(1<<0)  0b0000001 0      0         0       0       0       0       0
(1<<1)  0b0000010 0      0         0       0       0       0       0
(1<<2)  0b0000100 0      0         0       0       0       0       0
(1<<3)  0b0001000 0      0         0       0       0       0       0
(1<<4)  0b0010000 0      0         0       0       0       0       0
(1<<5)  0b0100000 0      0         0       0       0       0       0
(1<<6)  0b1000000 0      0         0       0       0       0       0
(1<<7)  0         0      0         0b00001 0       0       0       0
(1<<8)  0         0      0         0b00010 0       0       0       0
(1<<9)  0         0      0         0b00100 0       0       0       0
(1<<10) 0         0      0         0b01000 0       0       0       0
(1<<11) 0         0      0         0b10000 0       0       0       0
(1<<12) 0         0b001  0         0       0       0       0       0
(1<<13) 0         0b010  0         0       0       0       0       0
(1<<14) 0         0b100  0         0       0       0       0       0
(1<<15) 0         0      0         0       0b00001 0       0b00001 0
(1<<16) 0         0      0         0       0b00010 0       0b00010 0
(1<<17) 0         0      0         0       0b00100 0       0b00100 0
(1<<18) 0         0      0         0       0b01000 0       0b01000 0
(1<<19) 0         0      0         0       0b10000 0       0b10000 0
(1<<20) 0         0      0         0       0       0b00001 0       0b000000000001
(1<<21) 0         0      0         0       0       0b00010 0       0b000000000010
(1<<22) 0         0      0         0       0       0b00100 0       0b000000000100
(1<<23) 0         0      0         0       0       0b01000 0       0b000000001000
(1<<24) 0         0      0         0       0       0b10000 0       0b000000010000
(1<<25) 0         0      0b0000001 0       0       0       0       0b000000100000
(1<<26) 0         0      0b0000010 0       0       0       0       0b000001000000
(1<<27) 0         0      0b0000100 0       0       0       0       0b000010000000
(1<<28) 0         0      0b0001000 0       0       0       0       0b000100000000
(1<<29) 0         0      0b0010000 0       0       0       0       0b001000000000
(1<<30) 0         0      0b0100000 0       0       0       0       0b010000000000
(1<<31) 0         0      0b1000000 0       0       0       0       0b100000000000
*/
