// Digital circuit register_file.dig as structural Verilog
module register_file (
  input  [31:0] Din,
  input  we,
  input  [4:0] Rw,
  input  C,
  input  [4:0] Ra,
  input  [4:0] Rb,
  output [31:0] Da,
  output [31:0] Db
);

  wire demultiplexer_1_out_0, demultiplexer_1_out_1, demultiplexer_1_out_2, demultiplexer_1_out_3,
       demultiplexer_1_out_4, demultiplexer_1_out_5, demultiplexer_1_out_6, demultiplexer_1_out_7,
       demultiplexer_1_out_8, demultiplexer_1_out_9, demultiplexer_1_out_10, demultiplexer_1_out_11,
       demultiplexer_1_out_12, demultiplexer_1_out_13, demultiplexer_1_out_14, demultiplexer_1_out_15,
       demultiplexer_1_out_16, demultiplexer_1_out_17, demultiplexer_1_out_18, demultiplexer_1_out_19,
       demultiplexer_1_out_20, demultiplexer_1_out_21, demultiplexer_1_out_22, demultiplexer_1_out_23,
       demultiplexer_1_out_24, demultiplexer_1_out_25, demultiplexer_1_out_26, demultiplexer_1_out_27,
       demultiplexer_1_out_28, demultiplexer_1_out_29, demultiplexer_1_out_30, demultiplexer_1_out_31;
  wire [31:0] r0_q, r1_q, r2_q, r3_q, r4_q, r5_q, r6_q, r7_q, r8_q, r9_q, r10_q, r11_q, r12_q, r13_q, r14_q,
       r15_q, r16_q, r17_q, r18_q, r19_q, r20_q, r21_q, r22_q, r23_q, r24_q, r25_q, r26_q, r27_q, r28_q,
       r29_q, r30_q, r31_q;

  Demultiplexer #(.Selector_Bits(5)) demultiplexer_1 (
    .sel(Rw), .in(we), .out_0(demultiplexer_1_out_0), .out_1(demultiplexer_1_out_1),
    .out_2(demultiplexer_1_out_2), .out_3(demultiplexer_1_out_3), .out_4(demultiplexer_1_out_4),
    .out_5(demultiplexer_1_out_5), .out_6(demultiplexer_1_out_6), .out_7(demultiplexer_1_out_7),
    .out_8(demultiplexer_1_out_8), .out_9(demultiplexer_1_out_9), .out_10(demultiplexer_1_out_10),
    .out_11(demultiplexer_1_out_11), .out_12(demultiplexer_1_out_12), .out_13(demultiplexer_1_out_13),
    .out_14(demultiplexer_1_out_14), .out_15(demultiplexer_1_out_15), .out_16(demultiplexer_1_out_16),
    .out_17(demultiplexer_1_out_17), .out_18(demultiplexer_1_out_18), .out_19(demultiplexer_1_out_19),
    .out_20(demultiplexer_1_out_20), .out_21(demultiplexer_1_out_21), .out_22(demultiplexer_1_out_22),
    .out_23(demultiplexer_1_out_23), .out_24(demultiplexer_1_out_24), .out_25(demultiplexer_1_out_25),
    .out_26(demultiplexer_1_out_26), .out_27(demultiplexer_1_out_27), .out_28(demultiplexer_1_out_28),
    .out_29(demultiplexer_1_out_29), .out_30(demultiplexer_1_out_30), .out_31(demultiplexer_1_out_31));
  Register #(.Bits(32)) r0 (.D(Din), .C(C), .en(demultiplexer_1_out_0), .Q(r0_q));
  Register #(.Bits(32)) r1 (.D(Din), .C(C), .en(demultiplexer_1_out_1), .Q(r1_q));
  Register #(.Bits(32)) r2 (.D(Din), .C(C), .en(demultiplexer_1_out_2), .Q(r2_q));
  Register #(.Bits(32)) r3 (.D(Din), .C(C), .en(demultiplexer_1_out_3), .Q(r3_q));
  Register #(.Bits(32)) r4 (.D(Din), .C(C), .en(demultiplexer_1_out_4), .Q(r4_q));
  Register #(.Bits(32)) r5 (.D(Din), .C(C), .en(demultiplexer_1_out_5), .Q(r5_q));
  Register #(.Bits(32)) r6 (.D(Din), .C(C), .en(demultiplexer_1_out_6), .Q(r6_q));
  Register #(.Bits(32)) r7 (.D(Din), .C(C), .en(demultiplexer_1_out_7), .Q(r7_q));
  Register #(.Bits(32)) r8 (.D(Din), .C(C), .en(demultiplexer_1_out_8), .Q(r8_q));
  Register #(.Bits(32)) r9 (.D(Din), .C(C), .en(demultiplexer_1_out_9), .Q(r9_q));
  Register #(.Bits(32)) r10 (.D(Din), .C(C), .en(demultiplexer_1_out_10), .Q(r10_q));
  Register #(.Bits(32)) r11 (.D(Din), .C(C), .en(demultiplexer_1_out_11), .Q(r11_q));
  Register #(.Bits(32)) r12 (.D(Din), .C(C), .en(demultiplexer_1_out_12), .Q(r12_q));
  Register #(.Bits(32)) r13 (.D(Din), .C(C), .en(demultiplexer_1_out_13), .Q(r13_q));
  Register #(.Bits(32)) r14 (.D(Din), .C(C), .en(demultiplexer_1_out_14), .Q(r14_q));
  Register #(.Bits(32)) r15 (.D(Din), .C(C), .en(demultiplexer_1_out_15), .Q(r15_q));
  Register #(.Bits(32)) r16 (.D(Din), .C(C), .en(demultiplexer_1_out_16), .Q(r16_q));
  Register #(.Bits(32)) r17 (.D(Din), .C(C), .en(demultiplexer_1_out_17), .Q(r17_q));
  Register #(.Bits(32)) r18 (.D(Din), .C(C), .en(demultiplexer_1_out_18), .Q(r18_q));
  Register #(.Bits(32)) r19 (.D(Din), .C(C), .en(demultiplexer_1_out_19), .Q(r19_q));
  Register #(.Bits(32)) r20 (.D(Din), .C(C), .en(demultiplexer_1_out_20), .Q(r20_q));
  Register #(.Bits(32)) r21 (.D(Din), .C(C), .en(demultiplexer_1_out_21), .Q(r21_q));
  Register #(.Bits(32)) r22 (.D(Din), .C(C), .en(demultiplexer_1_out_22), .Q(r22_q));
  Register #(.Bits(32)) r23 (.D(Din), .C(C), .en(demultiplexer_1_out_23), .Q(r23_q));
  Register #(.Bits(32)) r24 (.D(Din), .C(C), .en(demultiplexer_1_out_24), .Q(r24_q));
  Register #(.Bits(32)) r25 (.D(Din), .C(C), .en(demultiplexer_1_out_25), .Q(r25_q));
  Register #(.Bits(32)) r26 (.D(Din), .C(C), .en(demultiplexer_1_out_26), .Q(r26_q));
  Register #(.Bits(32)) r27 (.D(Din), .C(C), .en(demultiplexer_1_out_27), .Q(r27_q));
  Register #(.Bits(32)) r28 (.D(Din), .C(C), .en(demultiplexer_1_out_28), .Q(r28_q));
  Register #(.Bits(32)) r29 (.D(Din), .C(C), .en(demultiplexer_1_out_29), .Q(r29_q));
  Register #(.Bits(32)) r30 (.D(Din), .C(C), .en(demultiplexer_1_out_30), .Q(r30_q));
  Register #(.Bits(32)) r31 (.D(Din), .C(C), .en(demultiplexer_1_out_31), .Q(r31_q));
  Multiplexer #(.Bits(32), .Selector_Bits(5)) multiplexer_1 (
    .sel(Ra), .in_0(r0_q), .in_1(r1_q), .in_2(r2_q), .in_3(r3_q), .in_4(r4_q), .in_5(r5_q), .in_6(r6_q),
    .in_7(r7_q), .in_8(r8_q), .in_9(r9_q), .in_10(r10_q), .in_11(r11_q), .in_12(r12_q), .in_13(r13_q),
    .in_14(r14_q), .in_15(r15_q), .in_16(r16_q), .in_17(r17_q), .in_18(r18_q), .in_19(r19_q), .in_20(r20_q),
    .in_21(r21_q), .in_22(r22_q), .in_23(r23_q), .in_24(r24_q), .in_25(r25_q), .in_26(r26_q), .in_27(r27_q),
    .in_28(r28_q), .in_29(r29_q), .in_30(r30_q), .in_31(r31_q), .out(Da));
  Multiplexer #(.Selector_Bits(5), .Bits(32)) multiplexer_2 (
    .sel(Rb), .in_0(r0_q), .in_1(r1_q), .in_2(r2_q), .in_3(r3_q), .in_4(r4_q), .in_5(r5_q), .in_6(r6_q),
    .in_7(r7_q), .in_8(r8_q), .in_9(r9_q), .in_10(r10_q), .in_11(r11_q), .in_12(r12_q), .in_13(r13_q),
    .in_14(r14_q), .in_15(r15_q), .in_16(r16_q), .in_17(r17_q), .in_18(r18_q), .in_19(r19_q), .in_20(r20_q),
    .in_21(r21_q), .in_22(r22_q), .in_23(r23_q), .in_24(r24_q), .in_25(r25_q), .in_26(r26_q), .in_27(r27_q),
    .in_28(r28_q), .in_29(r29_q), .in_30(r30_q), .in_31(r31_q), .out(Db));

  // Notes on the sheet:
  //   Replacement of the builtin register file with probes for every register to allow them to be read as measurement values.
endmodule

/* Test case:
	C      we     Din    Rw     Ra     Rb     Da     Db
# Initially empty, remain empty without stores
loop(i,32)
	0      0      (i)    (i)    (i)    (i)    0      0
	0      1      (i)    (i)    (i)    (i)    0      0
	C      0      (i)    (i)    (i)    (i)    0      0
end loop

# Store (5-i) in each register
loop(i, 32)
	C      1      (5-i)  (i)    0      0      5      5
end loop

# Read (5-i) from each register using s1 and s2
loop(i, 32)
	0      0      0      0      (i)    0      (5-i)  5
	0      0      0      0      0      (i)    5      (5-i)
end loop
*/
