// Digital circuit equals_zero.dig as structural Verilog
module equals_zero (
  input  X,
  output eq_0
);

  Comparator #(.generic("this.Bits=args.Bits;")) comparator_1 (.a(1'b0), .b(X), .eq(eq_0));  // open: gt, lt
endmodule

/* Code that sets the parameters or builds the circuit:
Bits := 32;
*/
